# Fritzing sketch circuitry (saved by Fritzing 1.0.6)
circuit board: 8.46667cm x 5.64444cm
breadboards: 1

parts:
  MCU1 = Raspberry Pi Zero
  Part1 = Adafruit I2S Mic - SPH0645 [part_number="Adafruit #3421"]
  Part3 = LCD1602-I2C
  Part4 = Adafruit MAX98357A I2S 3W Class D Amplifier [part_number="Adafruit #3006"]

nets:
  N1: MCU1.pin_1, MCU1.pin_17, Part1.VDD
  VCC: MCU1.pin_2, MCU1.pin_4, Part3.VCC, Part4.VIN
  N2: MCU1.pin_3, Part3.SDA
  N3: MCU1.pin_5, Part3.SCL
  GND: MCU1.pin_6, MCU1.pin_9, MCU1.pin_20, MCU1.pin_25, MCU1.pin_34, Part1.GND, Part3.GND, Part4.GND
  N4: MCU1.pin_12, Part1.BCLK, Part4.BCLK
  N5: MCU1.pin_35, Part1.WS, Part4.LRCLK
  N6: MCU1.pin_38, Part1.DATA
  N7: MCU1.pin_40, Part4.DIN

custom parts:
  Adafruit I2S Mic - SPH0645: For many microcontrollers, adding audio input is easy with one of our analog microphone breakouts. But as you get to bigger and better microcontrollers and microcomputers, you'll find that you don't always have an analog input, or maybe you want to avoid the noise that can seep in with an analog mic system. Once you get past 8-bit micros, you will often find an I2S peripheral, that can take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
  LCD1602-I2C: A standard character display, usually with 2x16 characters. Comes in many colors with LCM1602 IIC attached.
  Adafruit MAX98357A I2S 3W Class D Amplifier: Listen to this good news - we now have an all in one digital audio amp breakout board that works incredibly well with the Raspberry Pi! If you're looking for an easy and low cost way to get you digital sound files bumpin' then the MAX08357 I2S Amp Breakout is for you. It takes standard I2S digital audio input and, not only decodes it into analog, but also amplifies it directly into a speaker.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
